// Logisim project exam2.circ as structural Verilog: 3 circuits, main circuit FSM
module FSM (
  input  [1:0] \input ,
  output result
);

  wire clock_1_out;
  wire [1:0] register_1_q, state_transition_1_next_state;

  state_transition state_transition_1 (
    .current_state(register_1_q), .\input (\input ), .next_state(state_transition_1_next_state));
  Clock clock_1 (.out(clock_1_out));
  Register #(.width(2)) register_1 (
    .D(state_transition_1_next_state), .Q(register_1_q), .clk(clock_1_out));  // open: en, clr
  \output  output_1 (.in_1(register_1_q), .ouput(result));
endmodule

module state_transition (
  input  [1:0] current_state,
  input  [1:0] \input ,
  output [1:0] next_state
);

  wire and_1_out, and_2_out, and_3_out, and_4_out, not_1_out, not_2_out, not_3_out, not_4_out, not_5_out;

  not not_1 (not_1_out, current_state[1]);
  not not_2 (not_2_out, \input [0]);
  not not_3 (not_3_out, current_state[0]);
  not not_4 (not_4_out, \input [0]);
  and and_1 (and_1_out, not_1_out, current_state[0], not_2_out);
  and and_2 (and_2_out, current_state[1], not_3_out, not_4_out);
  and and_3 (and_3_out, current_state[1], \input [1], \input [0]);
  not not_5 (not_5_out, \input [1]);
  and and_4 (and_4_out, current_state[1], \input [0]);
  or or_1 (next_state[1], and_1_out, and_2_out, and_3_out);
  or or_2 (next_state[0], not_5_out, and_4_out);
endmodule

module \output  (
  input  [1:0] in_1,
  output ouput
);

  and and_1 (ouput, in_1[1], in_1[0]);
endmodule
