// Logisim project test1.circ as structural Verilog: 1 circuit, main circuit voter
module voter (
  input  i1,
  input  i2,
  input  i3,
  input  zhu,
  output out_5
);

  wire nand_1_out, nand_2_out, nand_3_out, nand_4_out;

  nand nand_1 (nand_1_out, i1, i2, i3);
  nand nand_2 (nand_2_out, i2, i3, zhu);
  nand nand_3 (nand_3_out, i1, i3, zhu);
  nand nand_4 (nand_4_out, i1, i2, zhu);
  nand nand_5 (out_5, nand_1_out, nand_2_out, nand_3_out, nand_4_out);
endmodule
