// Logisim project test2(1).circ as structural Verilog: 1 circuit, main circuit ALU
module ALU (
  input  [31:0] i1,
  input  [31:0] i2,
  input  [3:0] ALUOp,
  output [31:0] out_4
);

  wire comparator_1_lt, comparator_2_lt;
  wire [31:0] adder_1_out, and_1_out, bit_extender_1_out, bit_extender_2_out, divider_1_out,
       multiplier_1_out, nor_1_out, or_1_out, shifter_1_out, shifter_2_out, shifter_3_out, subtractor_1_out,
       xor_1_out;

  Comparator #(.width(32)) comparator_1 (.a(i1), .b(i2), .lt(comparator_1_lt));  // open: gt, eq
  Comparator #(.width(32), .mode("unsigned")) comparator_2 (.a(i1), .b(i2), .lt(comparator_2_lt));  // open: gt, eq
  Shifter #(.width(32)) shifter_1 (.in(i1), .\dist (i2[4:0]), .out(shifter_1_out));
  Shifter #(.width(32), .shift("ar")) shifter_2 (.in(i1), .\dist (i2[4:0]), .out(shifter_2_out));
  Shifter #(.width(32), .shift("lr")) shifter_3 (.in(i1), .\dist (i2[4:0]), .out(shifter_3_out));
  Multiplier #(.width(32)) multiplier_1 (.a(i1), .b(i2), .out(multiplier_1_out));  // open: cin, cout
  Divider #(.width(32)) divider_1 (.a(i1), .b(i2), .out(divider_1_out));  // open: upper, rem
  Adder #(.width(32)) adder_1 (.a(i1), .b(i2), .out(adder_1_out));  // open: cin, cout
  Subtractor #(.width(32)) subtractor_1 (.a(i1), .b(i2), .out(subtractor_1_out));  // open: bin, bout
  assign and_1_out = i1 & i2;  // AND_Gate and_1, 32 bits wide
  assign or_1_out = i1 | i2;  // OR_Gate or_1, 32 bits wide
  assign bit_extender_1_out = {{31{1'b0}}, comparator_1_lt};  // Bit_Extender bit_extender_1
  assign bit_extender_2_out = {{31{1'b0}}, comparator_2_lt};  // Bit_Extender bit_extender_2
  assign xor_1_out = i1 ^ i2;  // XOR_Gate xor_1, 32 bits wide
  assign nor_1_out = ~(i1 | i2);  // NOR_Gate nor_1, 32 bits wide
  Multiplexer #(.select(4), .width(32)) multiplexer_1 (
    .in0(shifter_1_out), .in1(shifter_2_out), .in2(shifter_3_out), .in3(multiplier_1_out),
    .in4(divider_1_out), .in5(adder_1_out), .in6(subtractor_1_out), .in7(and_1_out), .in8(or_1_out),
    .in9(xor_1_out), .in10(nor_1_out), .in11(bit_extender_1_out), .in12(bit_extender_2_out), .out(out_4),
    .sel(ALUOp));  // open: in13, in14, in15, en
endmodule
