// Logisim project test2.circ as structural Verilog: 1 circuit, main circuit responder
module responder (
  input  in_1,
  input  in_2,
  input  in_3,
  input  in_4,
  output [2:0] out_5
);

  wire and_1_out, d_ff_1_qn, d_ff_2_qn, d_ff_3_qn;

  D_Flip_Flop d_ff_1 (.clk(in_1), .D(in_4), .Q(out_5[0]), .Qn(d_ff_1_qn), .en(and_1_out));  // open: preset, reset
  D_Flip_Flop d_ff_2 (.clk(in_2), .D(in_4), .Q(out_5[1]), .Qn(d_ff_2_qn), .en(and_1_out));  // open: preset, reset
  D_Flip_Flop d_ff_3 (.clk(in_3), .D(in_4), .Q(out_5[2]), .Qn(d_ff_3_qn), .en(and_1_out));  // open: preset, reset
  and and_1 (and_1_out, d_ff_3_qn, d_ff_2_qn, d_ff_1_qn);
endmodule
