// Logisim project test2답.circ as structural Verilog: 1 circuit, main circuit responder
module responder (
  input  in_1,
  input  in_2,
  input  in_3,
  input  in_4,
  output [2:0] out_5
);

  wire and_1_out, and_2_out, and_3_out, clock_1_out, d_ff_1_q, nor_1_out, or_1_out;

  Clock clock_1 (.out(clock_1_out));
  or or_1 (or_1_out, clock_1_out, d_ff_1_q);
  and and_1 (and_1_out, nor_1_out, in_1);
  and and_2 (and_2_out, nor_1_out, in_2);
  and and_3 (and_3_out, nor_1_out, in_3);
  D_Flip_Flop d_ff_1 (.clk(or_1_out), .D(in_4), .Q(d_ff_1_q));  // open: Qn, preset, en, reset
  nor nor_1 (nor_1_out, out_5[0], out_5[1], out_5[2]);
  D_Flip_Flop d_ff_2 (.clk(and_1_out), .D(d_ff_1_q), .Q(out_5[2]));  // open: Qn, preset, en, reset
  D_Flip_Flop d_ff_3 (.clk(and_2_out), .D(d_ff_1_q), .Q(out_5[1]));  // open: Qn, preset, en, reset
  D_Flip_Flop d_ff_4 (.clk(and_3_out), .D(d_ff_1_q), .Q(out_5[0]));  // open: Qn, preset, en, reset
endmodule
