// Logisim project test3.circ as structural Verilog: 3 circuits, main circuit 2nmod5
module _2nmod5 (
  input  ln,
  output [2:0] result
);

  wire clock_1_out;
  wire [1:0] n2n_1_output, register_1_q;

  _2n u_2n_1 (.s(register_1_q), .\input (ln), .\output (n2n_1_output));
  Register #(.width(2)) register_1 (.D(n2n_1_output), .Q(register_1_q), .clk(clock_1_out));  // open: en, clr
  Clock clock_1 (.out(clock_1_out));
  \output  output_1 (.s(register_1_q), .\input (ln), .\output (result));
endmodule

module _2n (
  input  [1:0] s,
  input  \input ,
  output [1:0] \output 
);


  assign \output  = {s[0], \input };
endmodule

module \output  (
  input  [1:0] s,
  input  \input ,
  output [2:0] \output 
);

  wire and_2_out, and_3_out, not_1_out, not_2_out, not_3_out;

  not not_1 (not_1_out, \input );
  not not_2 (not_2_out, s[0]);
  not not_3 (not_3_out, \input );
  and and_1 (\output [2], s[0], not_1_out);
  and and_2 (and_2_out, not_2_out, not_3_out);
  and and_3 (and_3_out, s[0], \input );
  or or_1 (\output [0], and_2_out, and_3_out);

  assign \output [1] = \input ;
endmodule
