// Logisim project 3-1과제.circ as structural Verilog: 2 circuits, main circuit main
module main (
  input  A,
  input  B,
  input  C,
  input  D,
  input  E,
  output out_6
);

  wire main_1_out_13, main_2_out_13, main_3_out_13, main_4_out_13, n2_4decoder_1_out_3, n2_4decoder_1_out_4,
       n2_4decoder_1_out_5, n2_4decoder_1_out_6, not_1_out;

  or or_1 (out_6, main_1_out_13, main_2_out_13, main_3_out_13);
  not not_1 (not_1_out, 1'b1);
  _2_4decoder u_2_4decoder_1 (
    .A(A), .B(B), .out_3(n2_4decoder_1_out_3), .out_4(n2_4decoder_1_out_4), .out_5(n2_4decoder_1_out_5),
    .out_6(n2_4decoder_1_out_6));
  \_8_1데이터선택기_main  main_1 (
    .D7(1'b1), .D6(not_1_out), .D5(not_1_out), .D4(1'b1), .D3(1'b1), .D2(1'b1), .D1(1'b1), .D0(not_1_out),
    .A2(E), .A1(D), .A0(C), .Enable(n2_4decoder_1_out_3), .out_13(main_1_out_13));
  \_8_1데이터선택기_main  main_2 (
    .D7(not_1_out), .D6(1'b1), .D5(1'b1), .D4(not_1_out), .D3(not_1_out), .D2(1'b1), .D1(not_1_out),
    .D0(1'b1), .A2(E), .A1(D), .A0(C), .Enable(n2_4decoder_1_out_4), .out_13(main_2_out_13));
  \_8_1데이터선택기_main  main_3 (
    .D7(1'b1), .D6(not_1_out), .D5(1'b1), .D4(1'b1), .D3(1'b1), .D2(not_1_out), .D1(1'b1), .D0(not_1_out),
    .A2(E), .A1(D), .A0(C), .Enable(n2_4decoder_1_out_5), .out_13(main_3_out_13));
  \_8_1데이터선택기_main  main_4 (
    .D7(1'b1), .D6(1'b1), .D5(not_1_out), .D4(1'b1), .D3(not_1_out), .D2(1'b1), .D1(not_1_out), .D0(1'b1),
    .A2(E), .A1(D), .A0(C), .Enable(n2_4decoder_1_out_6), .out_13(main_4_out_13));
endmodule

// 2:4d
module _2_4decoder (
  input  A,
  input  B,
  output out_3,
  output out_4,
  output out_5,
  output out_6
);

  wire not_1_out, not_2_out;

  not not_1 (not_1_out, A);
  not not_2 (not_2_out, B);
  and and_1 (out_3, not_1_out, not_2_out);
  and and_2 (out_4, B, B, not_1_out);
  and and_3 (out_5, A, not_2_out);
  and and_4 (out_6, B, A);
endmodule
