// Logisim project 3비트 반가산기를 이용한 전가산기.circ as structural Verilog: 1 circuit, main circuit main
module main (
  input  Cin,
  input  [1:0] A,
  input  [1:0] B,
  output [1:0] sum,
  output Carry
);

  wire main_1_out_3, main_2_out_3;
  wire [1:0] main_1_out_4;
  wire [1:1] not_1_out;

  not not_1 (not_1_out[1], 1'b1);
  \_3비트_반가산기_main  main_1 (.A(A), .B(B), .out_3(main_1_out_3), .out_4(main_1_out_4));
  \_3비트_반가산기_main  main_2 (.A({not_1_out[1], Cin}), .B(main_1_out_4), .out_3(main_2_out_3), .out_4(sum));
  or or_1 (Carry, main_2_out_3, main_1_out_3);
endmodule
