// Logisim project 8-1데이터선택기.circ as structural Verilog: 1 circuit, main circuit main
module main (
  input  D7,
  input  D6,
  input  D5,
  input  D4,
  input  D3,
  input  D2,
  input  D1,
  input  D0,
  input  A2,
  input  A1,
  input  A0,
  input  Enable,
  output out_13
);

  wire and_1_out, and_2_out, and_3_out, and_4_out, and_5_out, and_6_out, and_7_out, and_8_out, not_1_out,
       not_2_out, not_3_out;

  not not_1 (not_1_out, A2);
  not not_2 (not_2_out, A1);
  not not_3 (not_3_out, A0);
  and and_1 (and_1_out, D7, not_1_out, not_2_out, not_3_out, Enable);
  and and_2 (and_2_out, D6, not_1_out, not_2_out, not_3_out, Enable);
  and and_3 (and_3_out, D5, not_1_out, not_2_out, not_3_out, Enable);
  and and_4 (and_4_out, D4, not_1_out, not_2_out, not_3_out, Enable);
  and and_5 (and_5_out, D3, A2, A1, A0, Enable);
  and and_6 (and_6_out, D2, A2, A1, A0, Enable);
  and and_7 (and_7_out, D1, A2, A1, A0, Enable);
  and and_8 (and_8_out, D0, A2, A1, A0, Enable);
  or or_1 (out_13, and_1_out, and_2_out, and_3_out, and_4_out, and_5_out, and_6_out, and_7_out, and_8_out);
endmodule
