// Logisim project exam2.circ as structural Verilog: 2 circuits, main circuit FSM
module FSM (
  input  [1:0] in_1,
  output out_2
);

  wire clock_1_out;
  wire [1:0] n123_1_out_3, register_1_q;

  _123 u_123_1 (.cur(register_1_q), .\input (in_1), .out_3(n123_1_out_3));
  Register #(.width(2)) register_1 (.D(n123_1_out_3), .Q(register_1_q), .clk(clock_1_out));  // open: en, clr
  Clock clock_1 (.out(clock_1_out));
  and and_1 (out_2, register_1_q[0], register_1_q[1]);
endmodule

module _123 (
  input  [1:0] cur,
  input  [1:0] \input ,
  output [1:0] out_3
);

  wire and_1_out, and_2_out, and_3_out, and_4_out, and_5_out, and_6_out, and_7_out, and_8_out, and_9_out,
       and_10_out, and_11_out, not_1_out, not_2_out, not_3_out, not_4_out, or_1_out;

  not not_1 (not_1_out, cur[0]);
  not not_2 (not_2_out, cur[1]);
  not not_3 (not_3_out, \input [0]);
  not not_4 (not_4_out, \input [1]);
  and and_1 (and_1_out, cur[1], cur[0]);
  and and_2 (and_2_out, cur[0], not_2_out);
  and and_3 (and_3_out, not_1_out, cur[1]);
  and and_4 (and_4_out, not_3_out, \input [1]);
  and and_5 (and_5_out, not_4_out, \input [0]);
  and and_6 (and_6_out, \input [1], \input [0]);
  or or_1 (or_1_out, and_2_out, and_3_out);
  and and_7 (and_7_out, and_2_out, and_4_out);
  and and_8 (and_8_out, and_4_out, and_4_out);
  and and_9 (and_9_out, and_3_out, and_6_out);
  and and_10 (and_10_out, or_1_out, and_8_out);
  and and_11 (and_11_out, and_1_out, and_6_out);
  or or_2 (out_3[1], and_7_out, and_11_out, and_10_out, and_9_out);
  or or_3 (out_3[0], and_5_out, and_11_out, and_9_out);
endmodule
