// Logisim project test1.circ as structural Verilog: 1 circuit, main circuit voter
module voter (
  input  _1,
  input  _2,
  input  _3,
  input  zuigao,
  output out_5
);

  wire and_1_out, and_2_out, and_3_out, or_1_out;

  and and_1 (and_1_out, _1, _2);
  and and_2 (and_2_out, _3, _2);
  and and_3 (and_3_out, _3, _1);
  or or_1 (or_1_out, and_1_out, and_2_out, and_3_out);
  and and_4 (out_5, or_1_out, zuigao);
endmodule
