// Logisim project test2.circ as structural Verilog: 1 circuit, main circuit responder
module responder (
  input  _1,
  input  _2,
  input  _3,
  input  judge,
  output [2:0] out_5
);

  wire and_1_out, clock_1_out, d_ff_1_q, d_ff_2_qn, d_ff_3_qn, d_ff_4_qn;

  Clock clock_1 (.out(clock_1_out));
  D_Flip_Flop d_ff_1 (.clk(clock_1_out), .D(judge), .Q(d_ff_1_q));  // open: Qn, preset, en, reset
  D_Flip_Flop d_ff_2 (.clk(_1), .D(d_ff_1_q), .Q(out_5[2]), .Qn(d_ff_2_qn), .en(and_1_out));  // open: preset, reset
  D_Flip_Flop d_ff_3 (.clk(_2), .D(d_ff_1_q), .Q(out_5[1]), .Qn(d_ff_3_qn), .en(and_1_out));  // open: preset, reset
  D_Flip_Flop d_ff_4 (.clk(_3), .D(d_ff_1_q), .Q(out_5[0]), .Qn(d_ff_4_qn), .en(and_1_out));  // open: preset, reset
  and and_1 (and_1_out, d_ff_2_qn, d_ff_3_qn, d_ff_4_qn);
endmodule
