// Logisim project test3.circ as structural Verilog: 2 circuits, main circuit 2nmod5
module _2nmod5 (
  input  in_1,
  output [2:0] out_2
);

  wire clock_1_out;
  wire [1:0] register_1_q;

  Register #(.width(2)) register_1 (.D({register_1_q[0], in_1}), .Q(register_1_q), .clk(clock_1_out));  // open: en, clr
  Clock clock_1 (.out(clock_1_out));
  \output  output_1 (.n(register_1_q), .in(in_1), .out_3(out_2));
endmodule

module \output  (
  input  [1:0] n,
  input  in,
  output [2:0] out_3
);

  wire and_1_out, and_2_out, not_1_out, not_2_out;

  not not_1 (not_1_out, in);
  not not_2 (not_2_out, n[0]);
  and and_1 (and_1_out, not_2_out, in);
  and and_2 (and_2_out, n[0], in);
  and and_3 (out_3[2], n[0], not_1_out);
  xnor xnor_1 (out_3[0], n[0], in);
  or or_1 (out_3[1], and_1_out, and_2_out);
endmodule
